# Fritzing sketch design (saved by Fritzing 0.9.5d)

parts:
  Part3 = Thumb Joystick
  Part2 = Arduino Uno (Rev3)
  U1 = WS2812 RGB LED matrix 8x8
  U2 = WS2812 RGB LED matrix 8x8
  VCC1 = Battery
  l = Momentary Switch [package=ksa_sealed_tac_switch]
  d = Momentary Switch [package=ksa_sealed_tac_switch]
  u = Momentary Switch [package=ksa_sealed_tac_switch]
  S1 = Taiway 100-SP-X-T1 SPDT Miniature Toggle Switch [part_number=100-SP-X-T1-0-0-B1-M2 package=THT]
  r = Momentary Switch [package=ksa_sealed_tac_switch]
  A1 = MH-FMD buzzer

nets:
  GND: Part3.GND, Part2.GND, U1.GND#0, VCC1.-, S1.L2, A1.Pin_3
  N1: Part3.SEL, Part2.A3
  N2: Part3.HORZ, Part2.A5/SCL
  N3: Part3.VERT, Part2.A4/SDA
  VCC: Part3.VCC, Part2.5V, U1.VCC#1, l.1, l.2, d.1, d.2, u.1, u.2, r.1, r.2, A1.Pin_1
  N4: Part2.D8, r.3, r.4
  N5: Part2.D10_PWM/SS, A1.Pin_2
  N6: Part2.D11_PWM/MOSI, U1.DIN
  N7: Part2.D2, l.3, l.4
  N8: Part2.D4, d.3, d.4
  N9: Part2.D7, u.3, u.4
  N10: Part2.VIN, S1.COM
  N11: U1.GND#4, U2.GND
  N12: U1.VCC#5, U2.VCC
  N13: U1.DOUT, U2.DIN
  N14: VCC1.+, S1.L1

custom parts:
  WS2812 RGB LED matrix 8x8: WS2812 matrix 8x8
  Battery: Your standard 2x 18650 battery pack (7,4 Volts)
  MH-FMD buzzer: MH-FMD buzzer.
